# Fritzing sketch module (saved by Fritzing 0.7.12b)
breadboards: 1

parts:
  Arduino1 = Arduino
  reset_button = Pushbutton [package="[THT]"]
  R1 = Resistor [tolerance=±5% resistance=220 package=THT]
  Part1 = USB LiPoly Charger
  I2C_Connection = Screw terminal - 2 pins [package=THT]
  Stand-in_for_Hall_sensor_1 = NPN-Transistor [package="TO92 [THT]"]
  R2 = Resistor [tolerance=±5% resistance=1.2k package=THT]
  Stand-in_for_Hall_sensor_2 = NPN-Transistor [package="TO92 [THT]"]
  R3 = Resistor [tolerance=±5% resistance=1.2k package=THT]
  S1 = Toggle Switch [package=THT]

nets:
  GND: Arduino1.GND, R1.Pin_1, Part1.GND, Stand-in_for_Hall_sensor_1.B, Stand-in_for_Hall_sensor_2.B
  N1: Arduino1.D8, reset_button.Pin_3, reset_button.Pin_4, R1.Pin_0
  N2: Arduino1.D3, Stand-in_for_Hall_sensor_2.C, R3.Pin_0
  N3: Arduino1.D2, Stand-in_for_Hall_sensor_1.C, R2.Pin_0
  N4: Arduino1.+5V, reset_button.Pin_1, reset_button.Pin_2
  N5: Arduino1.A4, I2C_Connection.pin1
  N6: Arduino1.A5, I2C_Connection.pin2
  N7: Part1.VBAT, S1.COM
  5V: Stand-in_for_Hall_sensor_1.E, R2.Pin_1, Stand-in_for_Hall_sensor_2.E, R3.Pin_1

notes:
  Not correct Sparkfun product.
  Using Hall IC Infineon TLE 4945 L
